# Fritzing sketch Drunk Darts (saved by Fritzing 0.9.2b)
breadboards: 1

parts:
  U1 = GAS_SENSOR [package=mq-3]
  R1 = Resistor [tolerance=±5% resistance=10k package="0603 [SMD]"]
  Grove1 = Grove 4 Digit Display  # not connected
  S3 = Pushbutton [package="[SMD]"]  # not connected
  Part2 = Arduino Uno (Rev3)
  C2 = Ceramic Capacitor [capacitance="100 nF" package="0805 [SMD, multilayer]"]
  C3 = Ceramic Capacitor [capacitance="100 nF" package="0805 [SMD, multilayer]"]
  R2 = Resistor [tolerance=±5% resistance=220 package=THT]
  R3 = Resistor [tolerance=±5% resistance=220 package="2512 [SMD]"]
  U2 = SWITCH_SPDT [package=kps-1290]
  R4 = Resistor [tolerance=±5% resistance=220 package="2512 [SMD]"]

nets:
  N1: U1.B1, R1.Pin_1, Part2.A0
  N2: U1.A1, U1.H1, Part2.5V, U2.P
  N3: U1.H2, R1.Pin_0, Part2.GND, C2.1, C3.0, R2.Pin_1, R3.Pin_0, R4.Pin_0
  N4: Part2.D13/SCK, U2.O, R4.Pin_1
  N5: Part2.D2, C2.0, R3.Pin_1
  N6: Part2.D3_PWM, C3.1, R2.Pin_0

notes:
  Grove 16x2 LED LCD Display
  MQ-3 Alcohol Sensor
  Green = Outer
  Yellow = Inner
